# Fritzing sketch TOFsensorDesignWPi (saved by Fritzing 0.9.3b)
breadboards: 1

parts:
  J3 = female pin header, 6 pins [form="♀ (female)"]
  Raspberry_Pi_1 = Raspberry Pi 3 [part_number=RPI-3-V1.2]

nets:
  N1: J3.pin1, J3.pin6, Raspberry_Pi_1.3v3
  N2: J3.pin3, Raspberry_Pi_1.GPIO2
  N3: J3.pin4, Raspberry_Pi_1.GPIO3
  N4: J3.pin5, Raspberry_Pi_1.GND

notes:
  XSHUT
  GPIO1
  SDA
  SCL
  GND
  VCC
